# Fritzing sketch Nineti_Assignment (saved by Fritzing 0.9.3b)
breadboards: 1

parts:
  MH-ET_LIVE_ESP32_DEVKIT1 = MH-ET LIVE ESP32 DEVKIT 38 pins
  DHT1 = DHT11 Humitidy and Temperature Sensor
  R1 = Resistor [tolerance=±5% resistance=10k package=THT]

nets:
  3V3: MH-ET_LIVE_ESP32_DEVKIT1.3V3, DHT1.VDD, R1.Pin_0
  N1: MH-ET_LIVE_ESP32_DEVKIT1.GND#64, DHT1.GND
  N2: MH-ET_LIVE_ESP32_DEVKIT1.IO2, DHT1.DATA, R1.Pin_1

custom parts:
  MH-ET LIVE ESP32 DEVKIT 38 pins: http://mh.nodebb.com/topic/2/mh-et-live-esp32-devkit
  DHT11 Humitidy and Temperature Sensor: DHT11 Humidity and Temperature Sensor
